# Fritzing sketch Diagrama (saved by Fritzing 0.9.3b)
breadboards: 1

parts:
  Componente1 = Arduino Uno (Rev3)
  J3 = Basic Servo
  LED1 = LED - 5mm [color="Red (633nm)" package="5 mm [THT]"]  # not connected
  R1 = Resistor [tolerance=±5% resistance=220 package=THT]
  M1 = fc-51 [package=THT]
  J2 = female pin header, 3 pins [form="♀ (female)"]

nets:
  N1: Componente1.D12/MISO, M1.pin1, J2.pin1
  GND: Componente1.GND, J3.gnd, R1.Pin_1, M1.pin2, J2.pin2
  N2: Componente1.D6_PWM, J3.pulse
  5V: Componente1.5V, J3.vcc, M1.pin3, J2.pin3
